# Fritzing sketch iot_collaboration (saved by Fritzing 0.9.2b)
breadboards: 1

parts:
  Part1 = Arduino Nano (Rev3.0)
  T1 = TMP36 Temperature Sensor [package="TO92 [THT]"]
  R1 = Photocell (LDR) [package=THT]

nets:
  N1: Part1.D2, R1.pin_1
  N2: T1.+Vs, R1.pin_0
